# Fritzing sketch fritzing-usb-ch375 - Copia (saved by Fritzing 0.9.3b)
breadboards: 1

parts:
  U2 = NodeMCU V1.0
  Componente2 = CH375
  Q3 = NPN-Transistor [part_number=2N2222 package="TO92 [THT]"]
  R5 = Resistor [tolerance=±5% resistance=1k package=THT]
  R6 = Resistor [tolerance=±5% resistance=1k package=THT]
  R8 = Resistor [tolerance=±5% resistance=1k package=THT]
  Q4 = NPN-Transistor [part_number=2N2222 package="TO92 [THT]"]
  R9 = Resistor [tolerance=±5% resistance=1k package=THT]

nets:
  N1: U2.D3, R5.Pin_0
  N2: U2.D4, Componente2.INT
  GND: U2.GND, Componente2.GND, Q3.E, Q4.E
  N3: U2.D6, Componente2.unknown#22
  VIN: U2.Vin, Componente2.VCC, R8.Pin_1, R9.Pin_1
  N4: Componente2.S, Q4.C, R9.Pin_0
  N5: Componente2.unknown#19, Componente2.unknown#20
  N6: Q3.B, R5.Pin_1
  N7: Q3.C, R6.Pin_0, R8.Pin_0
  N8: R6.Pin_1, Q4.B

custom parts:
  NodeMCU V1.0: ESP8266 based NodeMCU
